# Fritzing sketch hardware (saved by Fritzing 0.9.4)

parts:
  MCU1 = Raspberry Pi A+  # not connected
  Gizwits_WiFi_Witty_ESP-12F1 = Gizwits WiFi Witty ESP-12F  # not connected
  LED1 = RGB LED - (4 legs) [package="5 mm [THT]"]  # not connected
  Gizwits_WiFi_Witty_ESP-12F2 = Gizwits WiFi Witty ESP-12F
  LED2 = RGB LED - (4 legs) [package="5 mm [THT]"]

nets:
  N1: Gizwits_WiFi_Witty_ESP-12F2.GND, LED2.common_anode
  N2: Gizwits_WiFi_Witty_ESP-12F2.GPIO0, LED2.blue_cathode
  N3: Gizwits_WiFi_Witty_ESP-12F2.GPIO4, LED2.green_cathode
  N4: Gizwits_WiFi_Witty_ESP-12F2.GPIO5, LED2.red_cathode

notes:
  WiFi

custom parts:
  Raspberry Pi A+: The awesome Raspberry Pi ARM Board with 40 pin GPIO. Ready for special designed Raspberry Pi A+ Hat (Hardware attached (on) top). Jan 2018: Cloned from the B+ version, and modified to match the official I/O pin numbers with a totally new schematic.
